// Digital circuit 32位计算机.dig as structural Verilog
module \_32位计算机  (
  input  Clock,
  output [31:0] SP,
  output [3:0] STATE,
  output [7:0] IR,
  output [31:0] out_5,
  output [31:0] FP
);

  wire add_1_c_o, and_3_out, and_4_out, and_5_out, and_6_out, and_7_out, and_8_out, and_9_out, and_10_out,
       and_11_out, and_12_out, and_13_out, clock_t, CLR_IE, comparator_1_eq, comparator_2_eq,
       comparator_3_eq, CS_IVT, CS_KeyBoard, CS_RAM, CS_ROM, CS_Stack, CS_Telnet, CS_Terminal, DN_SP,
       driverinvsel_1_out, END_CYCLE, Flag_c, Flag_z, HALT, INC_PC, INT_REQ, INT_RET, INT_TAKE,
       keyboard_1_av, LD_FP, LD_IR, LD_MAR, LD_MDREXT, LD_MDRINT, LD_PC, LD_RFlags, LD_Rflags_Bus, LD_Rw,
       LD_SP, multiplexer_3_out, multiplexer_5_out, multiplexer_6_out, multiplexer_7_out, not_1_out,
       not_3_out, not_4_out, not_5_out, not_6_out, not_7_out, not_8_out, not_9_out, not_10_out, not_11_out,
       OE, OE_ALU, OE_FP, OE_INT_REQ, OE_MDREXT, OE_MDRINT, OE_PC, OE_Ra, OE_Rb, OE_Rflags, OE_SP, or_1_out,
       or_5_out, or_6_out, or_7_out, or_8_out, R_IE_q, SET_IE, sub_1_c_o, telnet_1_av, UP_SP, WE;
  wire [1:0] priorityencoder_1_num;
  wire [3:0] ADDR_Ra, ADDR_Rb, ADDR_Rw, MODE_ALU;
  wire [7:0] telnet_1_out;
  wire [15:0] driver_10_out, keyboard_1_d;
  wire [31:0] add_1_s, and_1_out, barrelshifter_1_out, CU_d, DEC_s, div_1_q, div_1_r, driver_1_out, INC_s,
       INT_ADDR, MAR_q, MDR_EXT_q, MDR_INT_q, multiplexer_1_out, multiplexer_4_out, nand_1_out, nor_1_out,
       not_2_out, or_3_out, RegFile_da, RegFile_db, sub_1_s, xnor_1_out, xor_1_out;
  wire [31:16] driver_10_out_2;
  wire [31:20] IR_q;
  wire [31:23] multiplexer_2_out;
  wire [33:0] CU_INT_d;
  wire [63:0] mul_1_mul;

  assign driver_1_out = OE_INT_REQ ? INT_ADDR : 32'bz;  // Driver driver_1
  CounterPreset #(.maxValue(15), .Bits(4)) u_STATE (
    .en(1'b1), .C(clock_t), .dir(1'b0), .in(4'b0000), .ld(1'b0), .clr(END_CYCLE), .out(STATE));  // open: ovf
  Register #(.Bits(32)) u_IR (.D(driver_1_out), .C(clock_t), .en(LD_IR), .Q({IR_q, ADDR_Ra, ADDR_Rb, ADDR_Rw, IR}));
  assign driver_1_out = OE_PC ? out_5 : 32'bz;  // Driver driver_2
  assign driver_1_out = OE_Rflags ? {{30{1'b0}}, Flag_c, Flag_z} : 32'bz;  // Driver driver_3
  Comparator #(.Bits(8)) u_HALT (.a(IR), .b(8'hf0), .eq(HALT));  // open: gt, lt
  assign driver_1_out = OE_Ra ? RegFile_da : 32'bz;  // Driver driver_4
  RegisterFile #(.AddrBits(4), .Bits(32)) RegFile (
    .Din(driver_1_out), .we(LD_Rw), .Rw(ADDR_Rw), .C(clock_t), .Ra(ADDR_Ra), .Rb(ADDR_Rb), .Da(RegFile_da),
    .Db(RegFile_db));
  assign driver_1_out = OE_Rb ? RegFile_db : 32'bz;  // Driver driver_5
  or or_1 (or_1_out, DN_SP, UP_SP);
  CounterPreset #(.Bits(32)) u_SP (
    .en(or_1_out), .C(clock_t), .dir(DN_SP), .in(driver_1_out), .ld(LD_SP), .clr(1'b0), .out(SP));  // open: ovf
  assign driver_1_out = OE_SP ? SP : 32'bz;  // Driver driver_6
  Register #(.Bits(32)) u_FP (.D(driver_1_out), .C(clock_t), .en(LD_FP), .Q(FP));
  assign driver_1_out = OE_FP ? FP : 32'bz;  // Driver driver_7
  CounterPreset #(.Bits(32), .isProgramCounter("true")) PC (
    .en(INC_PC), .C(clock_t), .dir(1'b0), .in(driver_1_out), .ld(LD_PC), .clr(1'b0), .out(out_5));  // open: ovf
  ROM #(.AddrBits(4), .Bits(34)) CU_INT (.A(STATE), .sel(INT_TAKE), .D(CU_INT_d));
  not not_1 (not_1_out, INT_TAKE);
  assign driver_1_out = OE_ALU ? multiplexer_4_out : 32'bz;  // Driver driver_8
  Comparator #(.Bits(8)) comparator_1 (.a(IR), .b(8'h33), .eq(comparator_1_eq));  // open: gt, lt
  Multiplexer #(.Bits(34)) multiplexer_1 (
    .sel(INT_TAKE), .in_0({34{1'b0}}), .in_1(CU_INT_d), .out({INT_RET, OE_INT_REQ, multiplexer_1_out}));
  ROM #(.AddrBits(12), .isProgramMemory("true"), .Bits(32)) CU (.A({IR, STATE}), .sel(not_1_out), .D(CU_d));
  assign driverinvsel_1_out = ~comparator_1_eq ? and_4_out : 1'bz;  // DriverInvSel driverinvsel_1
  or or_2 (INC_PC, multiplexer_2_out[23], driverinvsel_1_out);
  Add #(.Bits(32)) add_1 (.a(RegFile_da), .b(RegFile_db), .c_i(1'b0), .s(add_1_s), .c_o(add_1_c_o));
  Sub #(.Bits(32)) sub_1 (.a(RegFile_da), .b(RegFile_db), .c_i(1'b0), .s(sub_1_s), .c_o(sub_1_c_o));
  Mul #(.Bits(32)) mul_1 (.a(RegFile_da), .b(RegFile_db), .mul(mul_1_mul));
  Div #(.Bits(32)) div_1 (.a(RegFile_da), .b(RegFile_db), .q(div_1_q), .r(div_1_r));
  BarrelShifter #(.Bits(32)) barrelshifter_1 (.in(RegFile_da), .shift(RegFile_db[5:0]), .out(barrelshifter_1_out));
  assign and_1_out = RegFile_da & RegFile_db;  // And and_1, 32 bits wide
  assign nand_1_out = ~(RegFile_da & RegFile_db);  // NAnd nand_1, 32 bits wide
  assign or_3_out = RegFile_da | RegFile_db;  // Or or_3, 32 bits wide
  assign nor_1_out = ~(RegFile_da | RegFile_db);  // NOr nor_1, 32 bits wide
  assign xor_1_out = RegFile_da ^ RegFile_db;  // XOr xor_1, 32 bits wide
  assign xnor_1_out = ~(RegFile_da ^ RegFile_db);  // XNOr xnor_1, 32 bits wide
  assign not_2_out = ~RegFile_da;  // Not not_2, 32 bits wide
  Add #(.Bits(32)) INC (.a(RegFile_da), .b(32'h1), .c_i(1'b0), .s(INC_s));  // open: c_o
  Sub #(.Bits(32)) DEC (.a(RegFile_da), .b(32'h1), .c_i(1'b0), .s(DEC_s));  // open: c_o
  Multiplexer #(.Bits(32)) multiplexer_2 (
    .sel(INT_TAKE), .in_0(CU_d), .in_1(multiplexer_1_out),
    .out({multiplexer_2_out[31:30], MODE_ALU, WE, OE, multiplexer_2_out[23], SET_IE, CLR_IE, OE_ALU, OE_Rflags, OE_Rb, OE_Ra, OE_MDREXT, OE_MDRINT, OE_PC, OE_SP, OE_FP, LD_Rflags_Bus, LD_RFlags, LD_Rw, LD_IR, LD_MDREXT, LD_MDRINT, LD_MAR, LD_PC, LD_SP, LD_FP, UP_SP, DN_SP}));
  and and_2 (clock_t, Clock, not_3_out);
  not not_3 (not_3_out, HALT);
  or or_4 (END_CYCLE, and_4_out, multiplexer_2_out[31]);
  not not_4 (not_4_out, Flag_c);
  not not_5 (not_5_out, Flag_z);
  and and_3 (and_3_out, not_4_out, not_5_out);
  Multiplexer #(.Selector_Bits(4)) multiplexer_3 (
    .sel(IR_q[23:20]), .in_0(1'b0), .in_1(Flag_c), .in_2(Flag_z), .in_3(and_3_out), .in_4(not_6_out),
    .in_5(not_7_out), .in_6(not_8_out), .in_7(1'b0), .in_8(1'b0), .in_9(1'b0), .in_10(1'b0), .in_11(1'b0),
    .in_12(1'b0), .in_13(1'b0), .in_14(1'b0), .in_15(1'b0), .out(multiplexer_3_out));
  not not_6 (not_6_out, Flag_c);
  not not_7 (not_7_out, Flag_z);
  not not_8 (not_8_out, and_3_out);
  and and_4 (and_4_out, multiplexer_2_out[30], not_9_out);
  not not_9 (not_9_out, multiplexer_3_out);
  RS_FF R_IE (.S(SET_IE), .C(clock_t), .R(CLR_IE), .Q(R_IE_q));  // open: nQ
  assign driver_1_out = OE_MDRINT ? MDR_INT_q : 32'bz;  // Driver driver_9
  and and_5 (and_5_out, END_CYCLE, INT_REQ, R_IE_q);
  Register #(.Bits(32)) MDR_EXT (.D(driver_1_out), .C(clock_t), .en(LD_MDREXT), .Q(MDR_EXT_q));
  RS_FF rs_ff_1 (.S(and_5_out), .C(clock_t), .R(INT_RET), .Q(INT_TAKE));  // open: nQ
  Register #(.Bits(32)) MDR_INT (.D({driver_10_out_2, driver_10_out}), .C(clock_t), .en(LD_MDRINT), .Q(MDR_INT_q));
  assign {driver_10_out_2, driver_10_out} = OE_MDREXT ? MDR_EXT_q : 32'bz;  // Driver driver_10
  Multiplexer #(.Selector_Bits(4), .Bits(32)) multiplexer_4 (
    .sel(MODE_ALU), .in_0(add_1_s), .in_1(sub_1_s), .in_2(mul_1_mul[31:0]), .in_3(div_1_q),
    .in_4(barrelshifter_1_out), .in_5(and_1_out), .in_6(nand_1_out), .in_7(or_3_out), .in_8(nor_1_out),
    .in_9(xor_1_out), .in_10(xnor_1_out), .in_11(not_2_out), .in_12(INC_s), .in_13(DEC_s), .in_14(div_1_r),
    .in_15({32{1'b0}}), .out(multiplexer_4_out));
  Register #(.Bits(32)) MAR (.D(driver_1_out), .C(clock_t), .en(LD_MAR), .Q(MAR_q));
  Comparator #(.Bits(32)) comparator_2 (.a({32{1'b0}}), .b(multiplexer_4_out), .eq(comparator_2_eq));  // open: gt, lt
  Multiplexer multiplexer_5 (.sel(comparator_3_eq), .in_0(add_1_c_o), .in_1(sub_1_c_o), .out(multiplexer_5_out));
  Comparator #(.Bits(4)) comparator_3 (.a(MODE_ALU), .b(4'b0001), .eq(comparator_3_eq));  // open: gt, lt
  Multiplexer multiplexer_6 (
    .sel(not_10_out), .in_0(driver_1_out[1]), .in_1(multiplexer_5_out), .out(multiplexer_6_out));
  not not_10 (not_10_out, LD_Rflags_Bus);
  not not_11 (not_11_out, LD_Rflags_Bus);
  Multiplexer multiplexer_7 (.sel(not_11_out), .in_0(driver_1_out[0]), .in_1(comparator_2_eq), .out(multiplexer_7_out));
  or or_5 (or_5_out, LD_Rflags_Bus, LD_RFlags);
  or or_6 (or_6_out, LD_Rflags_Bus, LD_RFlags);
  Decoder #(.Selector_Bits(4)) decoder_1 (
    .sel(MAR_q[27:24]), .out_0(CS_ROM), .out_1(CS_RAM), .out_2(CS_Stack), .out_3(CS_IVT),
    .out_4(CS_KeyBoard), .out_5(CS_Terminal), .out_6(CS_Telnet));  // open: out_7, out_8, out_9, out_10, out_11, out_12, out_13, out_14, out_15
  Register register_1 (.D(multiplexer_7_out), .C(clock_t), .en(or_5_out), .Q(Flag_z));
  Register register_2 (.D(multiplexer_6_out), .C(clock_t), .en(or_6_out), .Q(Flag_c));
  and and_6 (and_6_out, CS_Terminal, WE);
  and and_7 (and_7_out, CS_Telnet, WE);
  and and_8 (and_8_out, CS_Telnet, OE);
  or or_7 (or_7_out, WE, OE);
  or or_8 (or_8_out, WE, OE);
  and and_9 (and_9_out, CS_KeyBoard, OE);
  EEPROM #(.AddrBits(24), .Bits(32)) ROM (
    .A(MAR_q[23:0]), .CS(CS_ROM), .WE(1'b0), .OE(OE), .D({driver_10_out_2, driver_10_out}));
  RAMSinglePortSel #(.AddrBits(24), .Bits(32)) RAM (
    .A(MAR_q[23:0]), .CS(and_10_out), .WE(WE), .OE(OE), .D({driver_10_out_2, driver_10_out}));
  and and_10 (and_10_out, CS_RAM, or_7_out);
  RAMSinglePortSel #(.AddrBits(24), .Bits(32)) Stack (
    .A(MAR_q[23:0]), .CS(CS_Stack), .WE(WE), .OE(OE), .D({driver_10_out_2, driver_10_out}));
  RAMSinglePortSel #(.AddrBits(24), .Bits(32)) IVT (
    .A(MAR_q[23:0]), .CS(and_11_out), .WE(WE), .OE(OE), .D({driver_10_out_2, driver_10_out}));
  and and_11 (and_11_out, CS_IVT, or_8_out);
  Keyboard keyboard_1 (.C(clock_t), .en(and_9_out), .D(keyboard_1_d), .av(keyboard_1_av));
  Terminal terminal_1 (.D(driver_10_out), .C(clock_t), .en(and_6_out));
  Telnet #(.port(8081)) telnet_1 (
    .in(driver_10_out[7:0]), .C(clock_t), .wr(and_7_out), .rd(and_8_out), .out(telnet_1_out), .av(telnet_1_av));
  and and_12 (and_12_out, CS_KeyBoard, OE);
  assign {driver_10_out_2, driver_10_out} = and_12_out ? {{16{1'b0}}, keyboard_1_d} : 32'bz;  // Driver driver_11
  and and_13 (and_13_out, CS_Telnet, OE);
  assign {driver_10_out_2, driver_10_out} = and_13_out ? {{24{1'b0}}, telnet_1_out} : 32'bz;  // Driver driver_12
  PriorityEncoder #(.Selector_Bits(2)) priorityencoder_1 (
    .in0(1'b0), .in1(1'b0), .in2(telnet_1_av), .in3(keyboard_1_av), .num(priorityencoder_1_num), .any(INT_REQ));
  Multiplexer #(.Selector_Bits(2), .Bits(32)) multiplexer_8 (
    .sel(priorityencoder_1_num), .in_0(32'h3000003), .in_1(32'h3000002), .in_2(32'h3000001),
    .in_3(32'h3000000), .out(INT_ADDR));

  // Notes on the sheet:
  //   Clock: Hz: 65536
  //   contents of CU_INT (hex, n*v repeats v):
  //   3c202020,3c004080,3e010002,3c002020,3c080080,3e010002,13c000020
  //   ,3d000040,2bc008010
  //   ALU
  //   contents of CU (hex, n*v repeats v):
  //   3c004020,3d800040,3c008100,bc000000,12*3c000000,3c004020,3d800040
  //   ,3c008100,bc000000,12*3c000000,3c004020,3d800040,3c008100,bc000000
  //   ,12*3c000000,3c004020,3d800040,3c008100,bc000000,12*3c000000,3c004020
  //   ,3d800040,3c008100,bc000000,12*3c000000,3c004020,3d800040,3c008100
  //   ,bc000000,12*3c000000,3c004020,3d800040,3c008100,bc000000,12*3c000000
  //   ,3c004020,3d800040,3c008100,bc000000,12*3c000000,3c004020,3d800040
  //   ,3c008100,bc000000,12*3c000000,3c004020,3d800040,3c008100,bc000000
  //   ,12*3c000000,3c004020,3d800040,3c008100,bc000000,12*3c000000,3c004020
  //   ,3d800040,3c008100,bc000000,12*3c000000,3c004020,3d800040,3c008100
  //   ,bc000000,12*3c000000,3c004020,3d800040,3c008100,bc000000,12*3c000000
  //   ,3c004020,3d800040,3c008100,bc000000,12*3c000000,3c004020,3d800040
  //   ,3c008100,bc000000,12*3c000000,3c004020,3d800040,3c008100,bc020200
  //   ,12*3c000000,3c004020,3d800040,3c008100,3c040020,3d000040,bc008200
  //   ,10*3c000000,3c004020,3d800040,3c008100,3c040020,3c020080,be010000
  //   ,10*3c000000,3c004020,3d800040,3c008100,3c004020,3d800040,3c008020
  //   ,3d000040,bc008200,8*3c000000,3c004020,3d800040,3c008100,3c004020
  //   ,3d800040,3c008020,3c020080,be010000,8*3c000000,3c004020,3d800040
  //   ,3c008100,3c804020,3d000040,bc008200,10*3c000000,3c004020,3d800040
  //   ,3c008100,3c804020,3d000040,bc008200,10*3c000000,3c004020,3d800040
  //   ,3c008100,100020,3d000040,bc008200,10*3c000000,3c004020,3d800040
  //   ,3c008100,bc000000,12*3c000000,3c004020,3d800040,3c008100,bc000000
  //   ,12*3c000000,3c004020,3d800040,3c008100,bc000000,12*3c000000,3c004020
  //   ,3d800040,3c008100,bc000000,12*3c000000,3c004020,3d800040,3c008100
  //   ,bc000000,12*3c000000,3c004020,3d800040,3c008100,bc000000,12*3c000000
  //   ,3c004020,3d800040,3c008100,bc000000,12*3c000000,3c004020,3d800040
  //   ,3c008100,bc000000,12*3c000000,3c004020,3d800040,3c008100,80100600
  //   ,12*3c000000,3c004020,3d800040,3c008100,84100600,12*3c000000,3c004020
  //   ,3d800040,3c008100,b0100200,12*3c000000,3c004020,3d800040,3c008100
  //   ,b4100200,12*3c000000,3c004020,3d800040,3c008100,88100600,12*3c000000
  //   ,3c004020,3d800040,3c008100,8c100600,12*3c000000,3c004020,3d800040
  //   ,3c008100,b8100600,12*3c000000,3c004020,3d800040,3c008100,90100600
  //   ,12*3c000000,3c004020,3d800040,3c008100,94100600,12*3c000000,3c004020
  //   ,3d800040,3c008100,98100600,12*3c000000,3c004020,3d800040,3c008100
  //   ,9c100600,12*3c000000,3c004020,3d800040,3c008100,a0100600,12*3c000000
  //   ,3c004020,3d800040,3c008100,a4100600,12*3c000000,3c004020,3d800040
  //   ,3c008100,a8100600,12*3c000000,3c004020,3d800040,3c008100,ac100600
  //   ,12*3c000000,3c004020,3d800040,3c008100,84000400,12*3c000000,3c004020
  //   ,3d800040,3c008100,3c004020,3d800040,bc008010,10*3c000000,3c004020
  //   ,3d800040,3c008100,40000000,3c004020,3d800040,bc008010,9*3c000000
  //   ,3c004020,3d800040,3c008100,bc020010,12*3c000000,3c004020,3d800040
  //   ,3c008100,40000000,bc020010,11*3c000000,3c004020,3d800040,3c008100
  //   ,3c804020,3d000040,3c002020,3c004080,3e010002,bc008010,7*3c000000
  //   ,3c004020,3d800040,3c008100,40000000,3c804020,3d000040,3c002020
  //   ,3c004080,3e010002,bc008010,6*3c000000,3c004020,3d800040,3c008100
  //   ,3c000001,3c002020,3d000040,bc008010,9*3c000000,3c004020,3d800040
  //   ,3c008100,3c804020,3d000040,3c002020,3c004080,3e010002,3c002020
  //   ,3c080080,3e010002,bc008010,4*3c000000,3c004020,3d800040,3c008100
  //   ,40000000,3c804020,3d000040,3c002020,3c004080,3e010002,3c002020
  //   ,3c080080,3e010002,bc008010,3c000000,3c000000,3c000000,3c004020
  //   ,3d800040,3c008100,3c400001,3c002020,3d000040,3c008801,3c002020
  //   ,3d000040,bc008010,6*3c000000,3c004020,3d800040,3c008100,bc400000
  //   ,12*3c000000,3c004020,3d800040,3c008100,bc200000,12*3c000000,3c004020
  //   ,3d800040,3c008100,bc000000,12*3c000000,3c004020,3d800040,3c008100
  //   ,bc000000,12*3c000000,3c004020,3d800040,3c008100,bc000000,12*3c000000
  //   ,3c004020,3d800040,3c008100,bc000000,12*3c000000,3c004020,3d800040
  //   ,3c008100,3c002020,3c020080,be010002,10*3c000000,3c004020,3d800040
  //   ,3c008100,3c000001,3c002020,3d000040,bc008200,9*3c000000,3c004020
  //   ,3d800040,3c008100,bc020008,12*3c000000,3c004020,3d800040,3c008100
  //   ,bc002200,12*3c000000,3c004020,3d800040,3c008100,bc001008,12*3c000000
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  //   contents of ROM (hex, n*v repeats v):
  //   e15,2000000,e0042,e0048,15,3000000,116,86,10012,15,1ffff38,115
  //   ,c8,34,be,15,1ffff37,115,0,10012,15,1ffff36,10012,3a,34,20,3b
  //   ,34,2f,34,74,f0,15,1ffff36,211,115,0,2102f,500031,2d,3a,211,2102f
  //   ,200031,28,3b,36,46,45,e43,f15,3,efe20,e0042,e49,f15,2,efe20,4e012
  //   ,e49,f15,1,efe20,5e012,e49,6e012,15,0,115,1,215,1ffff38,315,1ffff39
  //   ,a15,c7,10b10,c10,30,54,c1c20,ca02f,200031,60,c2d20,c3420,4611
  //   ,d511,5602f,600031,50,6d012,54012,b10,30,50,b002f,10b10,c10,200031
  //   ,54,e49,e611,e49,f15,1,efe20,e511,e49,f15,2,efe20,e411,44,47,36
  //   ,15,0,115,1ffff38,215,5000000,315,1,a15,c8,1b20,bb11,b2012,3020
  //   ,a02f,500031,7e,36,40,10040,20040,30040,40040,50040,60040,70040
  //   ,80040,90040,a0040,b0040,c0040,d0040,e0040,f0040,15,4000000,11
  //   ,115,1ffff37,1211,315,1ffff38,23220,2012,1211,15,1,20220,21012
  //   ,115,c8,2102f,500031,ad,115,1ffff36,1012,f41,e41,d41,c41,b41,a41
  //   ,941,841,741,641,541,441,341,241,141,41,39,30,c0,215,0,20012,315
  //   ,1,3020,13121,1202f,500031,c0,30,cc,36
endmodule
